// Logisim project CPU.circ as structural Verilog: 1 circuit, main circuit main
module main (
  input  in_1,
  input  in_2,
  input  in_3,
  input  in_4,
  input  in_5,
  input  in_6,
  input  in_7,
  input  in_8,
  input  in_9,
  input  in_10,
  input  in_11,
  input  in_12,
  input  in_13,
  input  in_14,
  input  in_15,
  input  in_16,
  input  in_17,
  input  in_18,
  input  in_19,
  input  in_20,
  input  in_21,
  input  in_22,
  input  in_23,
  input  in_24,
  input  in_25,
  input  in_26,
  input  in_27,
  input  in_28,
  input  in_29,
  input  in_30,
  input  in_31,
  input  in_32,
  input  in_33,
  input  in_34
);

  wire Clk, MAR_p7;
  wire [7:0] controlled_buffer_2_out, lTMP_dout, RA_2_dout, RA_3_dout, RA_dout, RB_dout;
  wire [15:0] controlled_buffer_1_out, PC_p7, SP_p7;

  Clock clock_1 (.out(Clk));
  _8bitReg lTMP (
    .Load(in_7), .Din(controlled_buffer_2_out), .Clk(Clk), .nCarryIn(1'b1), .Reset(in_3), .Dout(lTMP_dout));  // open: Up_nDown
  // Probe on lTMP_dout
  assign controlled_buffer_1_out[7:0] = in_5 ? lTMP_dout : 8'bz;  // Controlled_Buffer controlled_buffer_1
  _8bitReg RA (
    .Up_nDown(in_6), .Load(in_2), .Din(controlled_buffer_2_out), .Clk(Clk), .nCarryIn(in_4), .Reset(in_3),
    .Dout(RA_dout));
  // Probe on RA_dout
  // Probe on SP_p7
  // _16bitReg SP: pin names not known; wires that end beside it: in_15, in_11, controlled_buffer_1_out, in_13, Clk, in_3, SP_p7
  assign controlled_buffer_2_out = in_1 ? RA_dout : 8'bz;  // Controlled_Buffer controlled_buffer_2
  assign controlled_buffer_1_out = in_9 ? SP_p7 : 16'bz;  // Controlled_Buffer controlled_buffer_3
  _8bitReg RB (
    .Up_nDown(in_14), .Load(in_10), .Din(controlled_buffer_2_out), .Clk(Clk), .nCarryIn(in_12), .Reset(in_3),
    .Dout(RB_dout));
  // Probe on RB_dout
  assign controlled_buffer_2_out = in_29 ? controlled_buffer_1_out[15:8] : 8'bz;  // Controlled_Buffer controlled_buffer_4
  assign controlled_buffer_2_out = in_31 ? controlled_buffer_1_out[15:8] : 8'bz;  // Controlled_Buffer controlled_buffer_5
  assign controlled_buffer_2_out = in_8 ? RB_dout : 8'bz;  // Controlled_Buffer controlled_buffer_6
  _8bitReg RA_2 (
    .Up_nDown(in_22), .Load(in_18), .Din(controlled_buffer_2_out), .Clk(Clk), .nCarryIn(in_20), .Reset(in_3),
    .Dout(RA_2_dout));
  // Probe on RA_2_dout
  // Probe on PC_p7
  // _16bitReg PC: pin names not known; wires that end beside it: in_23, in_19, controlled_buffer_1_out, in_21, Clk, in_3, PC_p7
  assign controlled_buffer_2_out = in_16 ? RA_2_dout : 8'bz;  // Controlled_Buffer controlled_buffer_7
  assign controlled_buffer_1_out[7:0] = in_25 ? controlled_buffer_2_out : 8'bz;  // Controlled_Buffer controlled_buffer_8
  assign controlled_buffer_1_out = in_17 ? PC_p7 : 16'bz;  // Controlled_Buffer controlled_buffer_9
  _8bitReg RA_3 (
    .Up_nDown(in_30), .Load(in_26), .Clk(Clk), .nCarryIn(in_28), .Reset(in_3), .Dout(RA_3_dout));  // open: Din
  // Probe on RA_3_dout
  assign controlled_buffer_2_out = in_27 ? controlled_buffer_1_out[7:0] : 8'bz;  // Controlled_Buffer controlled_buffer_10
  assign controlled_buffer_2_out = in_24 ? RA_3_dout : 8'bz;  // Controlled_Buffer controlled_buffer_11
  // Probe on MAR_p7
  // _16bitReg MAR: pin names not known; wires that end beside it: in_34, in_32, controlled_buffer_1_out, in_33, Clk, in_3, MAR_p7

  // Other names for the same wires on the sheet: AhD = in_31; AlD = in_27; DAh = in_29; DAl = in_25; lTMPena = in_5;
  //   lTMPload = in_7; MAR_nCarry = in_33; MARload = in_32; MARu_nd = in_34; PC_nCarry = in_21; PCena = in_17;
  //   PCload = in_19; PCu_nd = in_23; RA_nCarry = in_4; RAena = in_1; RAload = in_2; RAu_nd = in_6; RB_nCarry = in_12;
  //   RBena = in_8; RBload = in_10; RBu_nd = in_14; RC_nCarry = in_20; RCena = in_16; RCload = in_18; RCu_nd = in_22;
  //   RD_nCarry = in_28; RDena = in_24; RDload = in_26; RDu_nd = in_30; Rst = in_3; SP_nCarry = in_13; SPena = in_9;
  //   SPload = in_11; SPu_nd = in_15
endmodule
